// Logisim project control_logic.circ as structural Verilog: 5 circuits, main circuit control_logic
module control_logic (
  input  [31:0] inst,
  input  BrEq,
  input  BrLt,
  output PCSel,
  output RegWEn,
  output [2:0] ImmSel,
  output BrUn,
  output ASel,
  output BSel,
  output [3:0] ALUSel,
  output MemRW,
  output [1:0] WBSel
);

  ALUSelectr aluselectr_1 (.opcode(inst[6:0]), .funct3(inst[14:12]), .funct7(inst[31:25]), .out_4(ALUSel));
  WBSelectr wbselectr_1 (.opcode(inst[6:0]), .out_2(WBSel));
  alotinone alotinone_1 (
    .BrEq(BrEq), .opcode(inst[6:0]), .BrLt(BrLt), .funct3(inst[14:12]), .funct7(inst[31:25]), .BrUn(BrUn),
    .Immsel(ImmSel), .RegWEn(RegWEn), .ASel(ASel), .pcSel(PCSel), .BSel(BSel), .MemRW(MemRW));

  // Other names for the same wires on the sheet: opcode[6:0] = inst[6:0]; funct3[2:0] = inst[14:12];
  //   funct7[6:0] = inst[31:25]

  // Notes on the sheet:
  //   INPUTS to your circuit
  //   DON'T CHANGE THE LOCATIONS OF THE INPUTS AND OUTPUTS!
  //   OUTPUT from your circuit
endmodule

module WBSelectr (
  input  [6:0] opcode,
  output [1:0] out_2
);

  wire comparator_1_eq, comparator_2_eq, comparator_3_eq, or_1_out;
  wire [1:0] bit_extender_1_out, bit_extender_2_out, multiplier_1_out;

  Comparator #(.width(7)) comparator_1 (.a(opcode), .b(7'b1101111), .eq(comparator_1_eq));  // open: gt, lt
  Comparator #(.width(7)) comparator_2 (.a(opcode), .b(7'b1100111), .eq(comparator_2_eq));  // open: gt, lt
  Comparator #(.width(5)) comparator_3 (.a(opcode[6:2]), .b({5{1'b0}}), .eq(comparator_3_eq));  // open: gt, lt
  or or_1 (or_1_out, comparator_1_eq, comparator_2_eq);
  assign bit_extender_1_out = {{1{1'b0}}, comparator_3_eq};  // Bit_Extender bit_extender_1
  assign bit_extender_2_out = {{1{1'b0}}, or_1_out};  // Bit_Extender bit_extender_2
  Multiplier #(.width(2)) multiplier_1 (.a(2'b10), .b(bit_extender_2_out), .out(multiplier_1_out));  // open: cin, cout
  Adder #(.width(2)) adder_1 (.a(bit_extender_1_out), .b(multiplier_1_out), .out(out_2));  // open: cin, cout
endmodule

module ALUSelectr (
  input  [6:0] opcode,
  input  [2:0] funct3,
  input  [6:0] funct7,
  output [3:0] out_4
);

  wire and_1_out, comparator_1_eq, comparator_2_eq, comparator_12_eq;
  wire [1:0] c7, comparator_7_eq;
  wire [2:0] comparator_9_eq;
  wire [3:0] AMS, comparator_3_eq, DSS, I_code, multiplexer_1_out, multiplexer_2_out, multiplexer_9_out,
       R_code, RA, SM;

  Multiplexer #(.select(3), .width(4), .enable("false")) multiplexer_1 (
    .in0(4'b0000), .in1(4'b0110), .in2(4'b0111), .in3(4'b1011), .in4(4'b0011), .in5(4'b0101), .in6(4'b0010),
    .in7(4'b0001), .out(multiplexer_1_out), .sel(funct3));
  Multiplexer #(.select(3), .width(4), .enable("false")) multiplexer_2 (
    .in0(4'b0000), .in1(4'b0110), .in2(4'b0111), .in4(4'b0011), .in5(4'b0101), .in6(4'b0010), .in7(4'b0001),
    .out(multiplexer_2_out), .sel(funct3));  // open: in3
  Comparator #(.width(4)) comparator_1 (.a(multiplexer_2_out), .b(4'b0101), .eq(comparator_1_eq));  // open: gt, lt
  Comparator #(.width(7)) comparator_2 (.a(funct7), .b({7{1'b0}}), .eq(comparator_2_eq));  // open: gt, lt
  Comparator #(.width(4)) comparator_3 (.a(multiplexer_1_out), .b(4'b0000), .eq(comparator_3_eq[0]));  // open: gt, lt
  Comparator #(.width(4)) comparator_4 (.a(multiplexer_1_out), .b(4'b0110), .eq(comparator_3_eq[1]));  // open: gt, lt
  Comparator #(.width(4)) comparator_5 (.a(multiplexer_1_out), .b(4'b0101), .eq(comparator_3_eq[2]));  // open: gt, lt
  Comparator #(.width(4)) comparator_6 (.a(multiplexer_1_out), .b(4'b0001), .eq(comparator_3_eq[3]));  // open: gt, lt
  Multiplexer #(.width(4), .enable("false")) multiplexer_3 (
    .in0(multiplexer_2_out), .in1(4'b0100), .out(I_code), .sel(and_1_out));
  and and_1 (and_1_out, comparator_1_eq, comparator_2_eq);
  Multiplexer #(.select(4), .width(4), .enable("false")) multiplexer_4 (
    .in0(multiplexer_1_out), .in1(AMS), .in2(SM), .in4(DSS), .in8(RA), .out(R_code), .sel(comparator_3_eq));  // open: in3, in5, in6, in7, in9, in10, in11, in12, in13, in14, in15
  Multiplexer #(.select(2), .width(4), .enable("false")) multiplexer_5 (
    .in0(4'b0000), .in1(4'b1010), .in2(4'b1100), .out(AMS), .sel(c7));  // open: in3
  Multiplexer #(.select(2), .width(4), .enable("false")) multiplexer_6 (
    .in0(4'b0110), .in1(4'b1110), .out(SM), .sel(c7));  // open: in2, in3
  Comparator #(.width(7)) comparator_7 (.a(opcode), .b(7'b0010011), .eq(comparator_7_eq[0]));  // open: gt, lt
  Comparator #(.width(7)) comparator_8 (.a(opcode), .b(7'b0110011), .eq(comparator_7_eq[1]));  // open: gt, lt
  Comparator #(.width(7)) comparator_9 (.a(funct7), .b({7{1'b0}}), .eq(comparator_9_eq[0]));  // open: gt, lt
  Comparator #(.width(7)) comparator_10 (.a(funct7), .b(7'b0000001), .eq(comparator_9_eq[1]));  // open: gt, lt
  Comparator #(.width(7)) comparator_11 (.a(funct7), .b(7'b0100000), .eq(comparator_9_eq[2]));  // open: gt, lt
  Multiplexer #(.select(2), .width(4), .enable("false")) multiplexer_7 (
    .in0(4'b0100), .in1(4'b1000), .in2(4'b0101), .out(DSS), .sel(c7));  // open: in3
  Multiplexer #(.select(2), .width(4), .enable("false")) multiplexer_8 (
    .in0(4'b0001), .in1(4'b1001), .out(RA), .sel(c7));  // open: in2, in3
  Comparator #(.width(7)) comparator_12 (.a(opcode), .b(7'b0110111), .eq(comparator_12_eq));  // open: gt, lt
  Multiplexer #(.select(2), .width(4), .enable("false")) multiplexer_9 (
    .in0(4'b0000), .in1(I_code), .in2(R_code), .out(multiplexer_9_out), .sel(comparator_7_eq));  // open: in3
  Multiplexer #(.select(3), .width(2), .enable("false")) multiplexer_10 (
    .in1(2'b00), .in2(2'b01), .in4(2'b10), .out(c7), .sel(comparator_9_eq));  // open: in0, in3, in5, in6, in7
  Multiplexer #(.width(4), .enable("false")) multiplexer_11 (
    .in0(multiplexer_9_out), .in1(4'b1101), .out(out_4), .sel(comparator_12_eq));
endmodule

module MemRWChecker (
  input  [4:0] immsel,
  output Mem_RW
);

  Comparator #(.width(5)) comparator_1 (.a(5'b01000), .b(immsel), .eq(Mem_RW));  // open: gt, lt
endmodule

module alotinone (
  input  BrEq,
  input  [6:0] opcode,
  input  BrLt,
  input  [2:0] funct3,
  input  [6:0] funct7,
  output BrUn,
  output [2:0] Immsel,
  output RegWEn,
  output ASel,
  output pcSel,
  output BSel,
  output MemRW
);

  wire and_1_out, and_2_out, and_3_out, and_4_out, BranchCode, comparator_2_eq, comparator_3_eq,
       comparator_8_eq, comparator_9_eq, comparator_10_eq, comparator_11_eq, comparator_12_eq,
       comparator_13_eq, comparator_14_eq, comparator_15_eq, Itype, not_1_out, or_1_out, or_3_out, or_4_out,
       or_5_out, or_7_out, or_8_out, or_9_out, Rtype, SBtype, UJtype, Utype;

  Comparator #(.width(7)) comparator_1 (.a(opcode), .b(7'b0110011), .eq(Rtype));  // open: gt, lt
  Comparator #(.width(7)) comparator_2 (.a(opcode), .b(7'b0000011), .eq(comparator_2_eq));  // open: gt, lt
  Comparator #(.width(7)) comparator_3 (.a(opcode), .b(7'b0010011), .eq(comparator_3_eq));  // open: gt, lt
  Comparator #(.width(7)) comparator_4 (.a(opcode), .b(7'b0100011), .eq(MemRW));  // open: gt, lt
  Comparator #(.width(7)) comparator_5 (.a(opcode), .b(7'b1100011), .eq(SBtype));  // open: gt, lt
  Comparator #(.width(7)) comparator_6 (.a(opcode), .b(7'b0110111), .eq(Utype));  // open: gt, lt
  Comparator #(.width(7)) comparator_7 (.a(opcode), .b(7'b1101111), .eq(UJtype));  // open: gt, lt
  Comparator #(.width(7)) comparator_8 (.a(opcode), .b(7'b1100111), .eq(comparator_8_eq));  // open: gt, lt
  or or_1 (or_1_out, comparator_2_eq, comparator_3_eq);
  or or_2 (Itype, or_1_out, comparator_8_eq);
  Comparator #(.width(3)) comparator_9 (.a(funct3), .b(3'b000), .eq(comparator_9_eq));  // open: gt, lt
  Comparator #(.width(3)) comparator_10 (.a(funct3), .b(3'b100), .eq(comparator_10_eq));  // open: gt, lt
  Comparator #(.width(3)) comparator_11 (.a(funct3), .b(3'b110), .eq(comparator_11_eq));  // open: gt, lt
  Comparator #(.width(3)) comparator_12 (.a(funct3), .b(3'b001), .eq(comparator_12_eq));  // open: gt, lt
  not not_1 (not_1_out, BrEq);
  and and_1 (and_1_out, comparator_9_eq, BrEq);
  and and_2 (and_2_out, comparator_10_eq, BrLt);
  and and_3 (and_3_out, comparator_11_eq, BrLt);
  and and_4 (and_4_out, comparator_12_eq, not_1_out);
  or or_3 (or_3_out, and_1_out, and_2_out);
  or or_4 (or_4_out, and_3_out, and_4_out);
  or or_5 (or_5_out, Itype, MemRW);
  or or_6 (BranchCode, or_3_out, or_4_out);
  or or_7 (or_7_out, MemRW, SBtype);
  or or_8 (or_8_out, Rtype, or_5_out);
  not not_2 (BSel, Rtype);
  not not_3 (RegWEn, or_7_out);
  not not_4 (ASel, or_8_out);
  and and_5 (BrUn, SBtype, funct3[1]);
  Comparator #(.width(7)) comparator_13 (.a(opcode), .b(7'b1101111), .eq(comparator_13_eq));  // open: gt, lt
  Comparator #(.width(7)) comparator_14 (.a(opcode), .b(7'b1100111), .eq(comparator_14_eq));  // open: gt, lt
  Comparator #(.width(7)) comparator_15 (.a(opcode), .b(7'b1100011), .eq(comparator_15_eq));  // open: gt, lt
  or or_9 (or_9_out, comparator_13_eq, comparator_14_eq);
  Multiplexer #(.enable("false")) multiplexer_1 (.in0(or_9_out), .in1(BranchCode), .out(pcSel), .sel(comparator_15_eq));
  Multiplexer #(.select(5), .width(3), .enable("false")) multiplexer_2 (
    .in0(3'b101), .in1(3'b000), .in2(3'b001), .in4(3'b010), .in8(3'b011), .in16(3'b100), .out(Immsel),
    .sel({UJtype, Utype, SBtype, MemRW, Itype}));  // open: in3, in5, in6, in7, in9, in10, in11, in12, in13, in14, in15, in17, in18, in19, in20, in21, in22, in23, in24, in25, in26, in27, in28, in29, in30, in31

  // Other names for the same wires on the sheet: Stype = MemRW; pc = pcSel
endmodule
