// Logisim project cpu.circ as structural Verilog: 2 circuits, main circuit main
module main (
  input  [31:0] INSTRUCTION,
  input  CLOCK,
  output [31:0] PROGRAM_COUNTER,
  output [31:0] ra,
  output [31:0] sp,
  output [31:0] t0,
  output [31:0] t1,
  output [31:0] t2,
  output [31:0] s0,
  output [31:0] s1,
  output [31:0] a0
);

  wire ASel, BrEq, BrLt, BrUn, BSel, DMEM_p1, DMEM_p2, DMEM_p7, loadchecker, MemRW, PCSel, RegWEn;
  wire [1:0] WBSel;
  wire [2:0] funct3, ImmSel;
  wire [3:0] ALUSel;
  wire [4:0] whichregiswhich_1_rd, whichregiswhich_1_rs1, whichregiswhich_1_rs2;
  wire [6:0] funct7;
  wire [7:0] multiplexer_4_out;
  wire [15:0] multiplexer_3_out;
  wire [24:0] newINSTRUCTION;
  wire [31:0] adder_1_out, ALU_Out, DataA, DataB, DataR, DataRin, DataRout, divider_1_rem, immediate, lb, lh,
       multiplexer_1_out, multiplexer_2_out, multiplexer_5_out, multiplexer_7_out, multiplexer_8_out, newPC;

  control_logic control_logic_1 (
    .BSel(BSel), .ASel(ASel), .BrUn(BrUn), .ImmSel(ImmSel), .RegWEn(RegWEn), .PCSel(PCSel), .BrLt(BrLt),
    .BrEq(BrEq), .inst({funct7, newINSTRUCTION[24:15], funct3, newINSTRUCTION[11:0]}), .ALUSel(ALUSel),
    .MemRW(MemRW), .WBSel(WBSel));
  Adder #(.width(32)) adder_1 (.a(PROGRAM_COUNTER), .b(32'h4), .out(adder_1_out));  // open: cin, cout
  Register #(.width(32)) PCFetch (.D(PROGRAM_COUNTER), .clk(CLOCK), .Q(newPC));  // open: en, clr
  Register #(.width(32)) PC (.D(multiplexer_1_out), .clk(CLOCK), .Q(PROGRAM_COUNTER));  // open: en, clr
  Multiplexer #(.width(32), .enable("false")) multiplexer_1 (
    .in0(adder_1_out), .in1(ALU_Out), .out(multiplexer_1_out), .sel(PCSel));
  imm_gen imm_gen_1 (
    .ImmSel(ImmSel), .inst({funct7, newINSTRUCTION[24:15], funct3, newINSTRUCTION[11:0]}), .imm(immediate));
  branch_comp branch_comp_1 (.BrEq(BrEq), .BrUn(BrUn), .rs1(DataA), .BrLt(BrLt), .rs2(DataB));
  Multiplexer #(.select(2), .width(32), .enable("false")) multiplexer_2 (
    .in0(ALU_Out), .in1(DataR), .in2(PROGRAM_COUNTER), .out(multiplexer_2_out), .sel(WBSel));  // open: in3
  WhichRegIsWhich whichregiswhich_1 (
    .instr({funct7, newINSTRUCTION[24:15], funct3, newINSTRUCTION[11:0]}), .RS1(whichregiswhich_1_rs1),
    .RS2(whichregiswhich_1_rs2), .RD(whichregiswhich_1_rd));
  assign lh = {{16{multiplexer_3_out[15]}}, multiplexer_3_out};  // Bit_Extender bit_extender_1
  Divider #(.width(32)) divider_1 (.a(ALU_Out), .b(32'h4), .rem(divider_1_rem));  // open: out, upper
  Multiplexer #(.select(2), .width(16), .enable("false")) multiplexer_3 (
    .in0(DataRin[15:0]), .in1(DataRin[31:16]), .in2(DataRin[31:16]), .in3(DataRin[31:16]),
    .out(multiplexer_3_out), .sel(divider_1_rem[1:0]));
  assign lb = {{24{multiplexer_4_out[7]}}, multiplexer_4_out};  // Bit_Extender bit_extender_2
  Multiplexer #(.select(2), .width(8), .enable("false")) multiplexer_4 (
    .in0(DataRin[7:0]), .in1(DataRin[15:8]), .in2(DataRin[23:16]), .in3(DataRin[31:24]),
    .out(multiplexer_4_out), .sel(divider_1_rem[1:0]));
  Multiplexer #(.width(32), .enable("false")) multiplexer_5 (
    .in0(INSTRUCTION), .in1(32'h13), .out(multiplexer_5_out), .sel(PCSel));
  Comparator #(.width(7)) comparator_1 (.a(newINSTRUCTION[6:0]), .b(7'b0000011), .eq(loadchecker));  // open: gt, lt
  Register #(.width(32)) inFetch (
    .D(multiplexer_5_out), .clk(CLOCK), .Q({funct7, newINSTRUCTION[24:15], funct3, newINSTRUCTION[11:0]}));  // open: en, clr
  // regfile_main RegFile: pin names not known; wires that end beside it: t0, t1, t2, s0, RegWEn, s1, a0, DataA, DataB
  Multiplexer #(.select(2), .width(32), .enable("false")) multiplexer_6 (
    .in0(lb), .in1(lh), .in2(DataRin), .out(DataRout), .sel(funct3[1:0]));  // open: in3
  Multiplexer #(.width(32), .enable("false")) multiplexer_7 (
    .in0(DataA), .in1(newPC), .out(multiplexer_7_out), .sel(ASel));
  Multiplexer #(.width(32), .enable("false")) multiplexer_8 (
    .in0(DataB), .in1(immediate), .out(multiplexer_8_out), .sel(BSel));
  // alu Arithmetic_Logic_Unit: pin names not known; wires that end beside it: DataB, multiplexer_7_out, multiplexer_8_out, ALUSel, ALU_Out
  Multiplexer #(.width(32), .enable("false")) multiplexer_9 (
    .in0(DataRin), .in1(DataRout), .out(DataR), .sel(loadchecker));
  // mem_main DMEM: pin names not known; wires that end beside it: DMEM_p1, DMEM_p2, ALU_Out, DataB, CLOCK, DMEM_p2, DMEM_p7, MemRW, DataRin

  // Other names for the same wires on the sheet: clk = CLOCK; opcode[6:0] = newINSTRUCTION[6:0];
  //   newINSTRUCTION (some bits) = {funct7, funct3}; PC_add_4[31:0] = PROGRAM_COUNTER

  // Notes on the sheet:
  //   Output
  //   IMEM (do **NOT** move this)
  //   Inputs
  //   It is OK to move the PC, RegFile, ALU, MEM, Branch Comp, Imm Gen, and Control Logic to wherever is most convenient for you when constructing your CPU, and to delete this text
  //   Inputs/Outputs for testing. Do **NOT** move these.
endmodule

module WhichRegIsWhich (
  input  [31:0] instr,
  output [4:0] RS1,
  output [4:0] RS2,
  output [4:0] RD
);


  assign RD = instr[11:7];
  assign RS1 = instr[19:15];
  assign RS2 = instr[24:20];
endmodule
