// Logisim project myalu.circ as structural Verilog: 1 circuit, main circuit alu
module alu (
  input  [31:0] A,
  input  [31:0] B,
  input  [3:0] ALUSel,
  output [31:0] Result
);

  wire comparator_1_eq, mulhIn;
  wire [0:0] slt7;
  wire [31:0] add0, and1, divu8, mul10, mulh, mulh14, mulhA, mulhB, mulhu11, multiplier_1_cout,
       negator_1_out, negator_2_out, negator_3_out, or2, remu9, sll6, sra5, srl4, sub12, subtractor_1_out,
       XOR3;

  Comparator #(.width(32)) comparator_1 (.a(mul10), .b({32{1'b0}}), .eq(comparator_1_eq));  // open: gt, lt
  Negator #(.width(32)) negator_1 (.in(A), .out(negator_1_out));
  Negator #(.width(32)) negator_2 (.in(B), .out(negator_2_out));
  Multiplier #(.width(32)) multiplier_1 (.a(mulhA), .b(mulhB), .cout(multiplier_1_cout));  // open: out, cin
  Multiplexer #(.width(32), .enable("false")) multiplexer_1 (
    .in0(mulh), .in1(mul10), .out(mulh14), .sel(comparator_1_eq));
  Multiplexer #(.width(32), .enable("false")) multiplexer_2 (.in0(A), .in1(negator_1_out), .out(mulhA), .sel(A[31]));
  Multiplexer #(.width(32), .enable("false")) multiplexer_3 (.in0(B), .in1(negator_2_out), .out(mulhB), .sel(B[31]));
  xor xor_1 (mulhIn, A[31], B[31]);
  Negator #(.width(32)) negator_3 (.in(multiplier_1_cout), .out(negator_3_out));
  Subtractor #(.width(32)) subtractor_1 (.a(negator_3_out), .b(32'h1), .out(subtractor_1_out));  // open: bin, bout
  Multiplexer #(.width(32), .enable("false")) multiplexer_4 (
    .in0(multiplier_1_cout), .in1(subtractor_1_out), .out(mulh), .sel(mulhIn));
  Multiplier #(.width(32)) multiplier_2 (.a(A), .b(B), .cout(mulhu11));  // open: out, cin
  Shifter #(.width(32), .shift("lr")) shifter_1 (.in(A), .\dist (B[4:0]), .out(srl4));
  Shifter #(.width(32), .shift("ar")) shifter_2 (.in(A), .\dist (B[4:0]), .out(sra5));
  Shifter #(.width(32)) shifter_3 (.in(A), .\dist (B[4:0]), .out(sll6));
  Comparator #(.width(32)) comparator_2 (.a(A), .b(B), .lt(slt7[0]));  // open: gt, eq
  Divider #(.width(32)) divider_1 (.a(A), .b(B), .out(divu8), .rem(remu9));  // open: upper
  Multiplier #(.width(32)) multiplier_3 (.a(A), .b(B), .out(mul10));  // open: cin, cout
  Subtractor #(.width(32)) subtractor_2 (.a(A), .b(B), .out(sub12));  // open: bin, bout
  Multiplexer #(.select(4), .width(32), .enable("false")) multiplexer_5 (
    .in0(add0), .in1(and1), .in2(or2), .in3(XOR3), .in4(srl4), .in5(sra5), .in6(sll6),
    .in7({{31{1'b0}}, slt7[0]}), .in8(divu8), .in9(remu9), .in10(mul10), .in11(mulhu11), .in12(sub12),
    .in13(B), .in14(mulh14), .out(Result), .sel(ALUSel));  // open: in15
  Adder #(.width(32)) adder_1 (.a(A), .b(B), .out(add0));  // open: cin, cout
  assign and1 = A & B;  // AND_Gate and_1, 32 bits wide
  assign or2 = A | B;  // OR_Gate or_1, 32 bits wide
  assign XOR3 = A ^ B;  // XOR_Gate xor_2, 32 bits wide

  // Notes on the sheet:
  //   INPUTS to your circuit
  //   DON'T CHANGE THE LOCATIONS OF THE INPUTS AND OUTPUTS!
  //   OUTPUT from your circuit
endmodule
