// Logisim project cpu-edgetegration2.circ as structural Verilog: 1 circuit, main circuit main
module main (
  output [31:0] ra,
  output [31:0] sp,
  output [31:0] t0,
  output [31:0] t1,
  output [31:0] t2,
  output [31:0] s0,
  output [31:0] s1,
  output [31:0] a0,
  output [31:0] Requested_Address,
  output [31:0] Requested_Instruction,
  output [15:0] Time_Step,
  output halt
);

  wire clk;

  Clock clock_1 (.out(clk));
  // Probe on Requested_Address
  ROM #(.addrWidth(14), .dataWidth(32)) rom_1 (.addr(Requested_Address[15:2]), .data(Requested_Instruction));
  cpu_main main_1 (
    .INSTRUCTION(Requested_Instruction), .CLOCK(clk), .ra(ra), .sp(sp), .t0(t0), .t1(t1), .t2(t2), .s0(s0),
    .s1(s1), .a0(a0), .PROGRAM_COUNTER(Requested_Address));
  // Probe on Requested_Instruction
  Counter #(.width(16), .max('hffff)) counter_1 (.clk(clk), .Q(Time_Step));  // open: clr, load, up, count, D, carry
  Comparator #(.width(16)) comparator_1 (.a(Time_Step), .b(16'h90a), .eq(halt));  // open: gt, lt

  // Other names for the same wires on the sheet: fetch_addr[31:0] = Requested_Address;
  //   Instruction[31:0] = Requested_Instruction

  // Notes on the sheet:
  //   contents of rom_1 (hex, n*v repeats v):
  //   00150493 00150313 00150513 00150093 00150413 00150393 00150113 00150293 009403B3 00155333 0210B3B3
  //   007323B3 002360B3 00751433 02943533 0083D2B3 4013D433 006340B3 009102B3 00808433 02A494B3 001550B3
  //   02A29333 005462B3 02110333 405403B3 001280B3 406282B3 40738333 026084B3 408553B3 00938533 002350B3
  //   007472B3 006440B3 027100B3 007480B3 021530B3 00A39533 007300B3 00751533 00748433 007340B3 401400B3
  //   00A2A3B3 40928133 009284B3 021110B3 006383B3 028402B3 001463B3 021394B3 0024C433 001474B3 408303B3
  //   006480B3 0290B433 00728133 02839433 025302B3 405403B3 007472B3 00140533 406282B3 00A4F0B3 00541133
  //   00151433 00A444B3 026512B3 002503B3 007103B3 00948133 4010D3B3 0094D2B3 0070C3B3 0023E333 00A082B3
  //   02738433 021532B3 002303B3 007480B3 00A503B3 40508333 005090B3 40945133 0063F3B3 00146533 02628533
  //   005503B3 00738133 008084B3 0050A533 4050D433 008402B3 028402B3 00A384B3 028333B3 00240133 02748533
  //   00A0E2B3 0094A333 00232433 007302B3 00737133 00712133 008514B3 00928133 001292B3 02110333 008102B3
  //   02A08533 008514B3 0250B133 00950333 00A28133 02250533 026512B3 40915133 0022D133 0064A4B3 002382B3
  //   40515133 0092A333 00657433 02A41533 00845433 0254B4B3 00A2A3B3 401352B3 0073C3B3 40608333 40908433
  //   40540133 00748533 028493B3 00955333 0052E4B3 40850533 002350B3 00737133 0062D0B3 005473B3 0052E4B3
  //   026092B3 401454B3 005422B3 00A0E433 00940433 02833133 008303B3 002290B3 40A450B3 00A384B3 402300B3
  //   00654333 0094E4B3 40810533 00728133 00930533 0050A533 026402B3 0012A433 02729333 02650333 006283B3
  //   02133333 0083E2B3 00A142B3 009283B3 02A512B3 407450B3 00A57433 001170B3 0260B2B3 40115333 00639333
  //   00A0F4B3 005084B3 00A162B3 002140B3 0052E4B3 40928333 40535533 00A454B3 00148333 00929333 0012A433
  //   002080B3 00148433 0023D133 002280B3 029280B3 40840133 00110433 009090B3 0073D4B3 001480B3 00A4A333
  //   007400B3 002292B3 406104B3 009280B3 00808533 008454B3 009352B3 007292B3 00844433 0073D533 02640333
  //   0073D533 002114B3 02513533 005090B3 00217333 005502B3 02153333 00528433 4053D0B3 40508333 02230133
  //   02830533 00608533 40A50433 02548133 00915333 00946433 02153333 40A10133 007102B3 005302B3 4070D0B3
  //   002300B3 008463B3 0093A333 02830533 408303B3 009300B3 40908433 02841533 00148433 002100B3 02A41533
  //   005084B3 4054D2B3 002402B3 002504B3 008303B3 02110333 00A0E2B3 00A454B3 02528133 0013E2B3 408150B3
  //   00637133 005342B3 0252B533 00A0D133 4082D2B3 002473B3 40210433 0263B0B3 028313B3 001302B3 40115333
  //   0274B433 02528133 00728433 005480B3 0050A0B3 0080D0B3 00708433 00511533 00737433 0093A333 002440B3
  //   02713133 00550133 02709133 00A360B3 009454B3 0014E133 00550533 02A31433 00A50133 0050D2B3 006383B3
  //   00552133 00930333 0084E2B3 0092D533 00A520B3 0083D2B3 00850433 00828533 0063E533 0074F3B3 0024C2B3
  //   001463B3 005303B3 0020F433 40238433 029133B3 00A294B3 00A3A3B3 0050F133 4014D2B3 026102B3 025302B3
  //   00A3C2B3 0090C4B3 0062E533 00A142B3 00848333 0264B533 027484B3 00A3F4B3 00915533 401280B3 02513533
  //   00A28133 005383B3 005503B3 002482B3 0084E0B3 0070D2B3 009280B3 0212B3B3 00629433 0070D0B3 00A0A133
  //   006303B3 406552B3 00A464B3 00528133 0212B533 00A082B3 007440B3 00844333 00534333 008383B3 00A094B3
  //   005564B3 00950533 0050D333 00708433 0063A2B3 02943533 0052A533 00938333 005484B3 02930433 009094B3
  //   00246533 002303B3 00A38133 002284B3 00614333 00A48433 00A0D133 00649533 005422B3 00712433 002140B3
  //   02740533 02A502B3 0084E133 00A0D133 007163B3 0070D2B3 02740533 02638333 00A122B3 001302B3 028500B3
  //   00A38133 00639333 0053E333 0094D0B3 0024A3B3 00917433 0094D3B3 0050D2B3 00951133 0094D3B3 002490B3
  //   00541133 02529133 00915333 00110433 408400B3 022414B3 40215533 00257433 40828333 0210B3B3 00A373B3
  //   00236533 00132133 0064F433 021533B3 0080D133 001480B3 00A4F0B3 0080F133 001550B3 0053A2B3 00240333
  //   027103B3 001382B3 002284B3 0282B4B3 40935333 0010E3B3 006340B3 00548333 0014E133 005374B3 005422B3
  //   00550533 006124B3 02628433 00A454B3 005422B3 006342B3 40738333 00939133 029532B3 40540133 02729133
  //   4054D2B3 021110B3 40945133 002303B3 40738333 027083B3 001104B3 008084B3 00A48133 409102B3 002280B3
  //   009394B3 001373B3 00830433 02633533 0063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
  //   YOUR CPU SHOULD FIT IN HERE!
  //   Instruction Memory
  //   Halts Execution After Constant # of Clock Cycles
  //   Constant
endmodule
